# Fritzing sketch sensors_wiring (saved by Fritzing 0.9.3b)
circuit board: 8.46667cm x 5.64444cm
breadboards: 1

parts:
  Part1 = Arduino Mega 2560 (Rev3)-TopMount
  DC_Mot_Enc1 = DC Motor with two-phase hall-encoder [part_number=VT-E-G25A-06-177E]
  SERVO1 = Adafruit Feedback Servo (small)
  S1 = H-Bridge with L298N
  Part2 = VL530X Time of Flight Distance Sensor [part_number="tonetoys #3317"]
  Part3 = VL530X Time of Flight Distance Sensor [part_number="tonetoys #3317"]
  Part4 = VL530X Time of Flight Distance Sensor [part_number="tonetoys #3317"]
  LED1 = LED - 5mm [color="Red (633nm)" package="5 mm [THT]"]
  R1 = Resistor [tolerance=±5% resistance=220 package=THT]

nets:
  N1: Part1.D21/SCL, Part2.SCL, Part3.SCL, Part4.SCL
  N2: Part1.D20/SDA, Part2.SDA, Part3.SDA, Part4.SDA
  N3: Part1.D10_PWM, LED1.anode, R1.Pin_0, R1.Pin_1
  N4: Part1.D9_PWM, SERVO1.Signal
  N5: Part1.D8_PWM, Part4.XSHUT
  GND: Part1.GND, SERVO1.Ground, S1.GND, Part2.GND, Part3.GND, Part4.GND, LED1.cathode
  N6: Part1.D3_PWM, S1.ENA
  N7: Part1.D4_PWM, S1.IN1
  N8: Part1.D5_PWM, S1.IN2
  N9: Part1.D6_PWM, Part3.XSHUT
  N10: Part1.D7_PWM, Part2.XSHUT
  N11: DC_Mot_Enc1.pin1, S1.M1-01
  N12: DC_Mot_Enc1.pin6, S1.M1-02, S1.M2-02, S1.ENA-5V

custom parts:
  Arduino Mega 2560 (Rev3)-TopMount: Arduino Mega 2560 (Rev3) for Top PCB Mount. The PCB view of the Arduino Mega 2560 (Rev3) in Arduino Bin flipped upside down with the text flipped back so as to be readable. Other views haven't changed Protruding component position is outlined to provide indication of part contact. Number in component outline is mm of protrusion of the component from the Mega PCB. Subtract the number from the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
  Adafruit Feedback Servo (small): Adafruit Feedback Servo (Small)
  H-Bridge with L298N: h-bridge
  VL530X Time of Flight Distance Sensor: Time of flight sensor
