# Fritzing sketch wiring_1 (saved by Fritzing 0.9.3b)
circuit board: 8.46667cm x 5.64444cm
breadboards: 1

parts:
  Part1 = Arduino Mega 2560 (Rev3)-TopMount
  DC_Mot_Enc1 = DC Motor with two-phase hall-encoder [part_number=VT-E-G25A-06-177E]
  SERVO1 = Adafruit Feedback Servo (small)
  S1 = H-Bridge with L298N

nets:
  N1: Part1.D9_PWM, SERVO1.Signal
  GND: Part1.GND, SERVO1.Ground, S1.GND
  N2: Part1.D3_PWM, S1.ENA
  N3: Part1.D4_PWM, S1.IN1
  N4: Part1.D5_PWM, S1.IN2
  N5: DC_Mot_Enc1.pin1, S1.M1-01
  N6: DC_Mot_Enc1.pin6, S1.M1-02, S1.M2-02, S1.ENA-5V

custom parts:
  Arduino Mega 2560 (Rev3)-TopMount: Arduino Mega 2560 (Rev3) for Top PCB Mount. The PCB view of the Arduino Mega 2560 (Rev3) in Arduino Bin flipped upside down with the text flipped back so as to be readable. Other views haven't changed Protruding component position is outlined to provide indication of part contact. Number in component outline is mm of protrusion of the component from the Mega PCB. Subtract the number from the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
  Adafruit Feedback Servo (small): Adafruit Feedback Servo (Small)
  H-Bridge with L298N: h-bridge
