# Fritzing sketch wiring_1 (saved by Fritzing 0.9.3b)
circuit board: 8.46667cm x 5.64444cm
breadboards: 1

parts:
  A1 = Raspberry Pi 5  # not connected
  Part1 = Arduino Mega 2560 (Rev3)-TopMount
  S1 = H-Bridge with L298N
  VCC1 = Battery  # not connected
  Part3 = VL530X Time of Flight Distance Sensor [part_number="tonetoys #3317"]  # not connected
  DC_Mot_Enc1 = DC Motor with two-phase hall-encoder [part_number=VT-E-G25A-06-177E]
  SERVO1 = Adafruit Feedback Servo (small)

nets:
  N1: Part1.D19/RX1, DC_Mot_Enc1.pin3
  N2: Part1.D18/TX1, DC_Mot_Enc1.pin4
  N3: Part1.D9_PWM, SERVO1.Signal
  N4: Part1.5V, DC_Mot_Enc1.pin5
  N5: Part1.D3_PWM, S1.ENA
  N6: Part1.D4_PWM, S1.IN1
  N7: Part1.D5_PWM, S1.IN2
  N8: S1.GND, SERVO1.Ground
  N9: S1.M1-01, DC_Mot_Enc1.pin1
  N10: S1.M1-02, S1.M2-02, S1.ENA-5V, DC_Mot_Enc1.pin6

custom parts:
  Raspberry Pi 5: The RPi5, a faster version of the awesome Raspberry Pi4B ARM Board with 40 pin gpio.
  Arduino Mega 2560 (Rev3)-TopMount: Arduino Mega 2560 (Rev3) for Top PCB Mount. The PCB view of the Arduino Mega 2560 (Rev3) in Arduino Bin flipped upside down with the text flipped back so as to be readable. Other views haven't changed Protruding component position is outlined to provide indication of part contact. Number in component outline is mm of protrusion of the component from the Mega PCB. Subtract the number from the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
  H-Bridge with L298N: h-bridge
  VL530X Time of Flight Distance Sensor: Time of flight sensor
  Adafruit Feedback Servo (small): Adafruit Feedback Servo (Small)
